// Logisim project sap1_1.circ as structural Verilog: 1 circuit, main circuit main
module main (
);

  wire A_sw1, A_sw2, A_sw3, A_sw4, and_1_out, C1_q1, C1_q2, C2_q1, C2_q2, C4_g4, C4_q1, C4_q2, C4_q3, C5_y1,
       C5_y2, C5_y3, C5_y4, C6_not_do1, C6_not_do2, C6_not_do3, C6_not_do4, C7_not_do1, C7_not_do2,
       C7_not_do3, C7_not_do4, C8_g4, C8_q1, C8_q2, C8_q3, C10_g4, C10_q1, C10_q2, C10_q3, C11_g4, C11_q1,
       C11_q2, C11_q3, C14_pin1, C14_pin3, C14_pin4, C14_pin6, C14_pin8, C14_pin9, C14_pin11, C14_pin12,
       C15_pin3, C15_pin6, C15_pin8, C15_pin11, C16_e1, C16_e2, C16_e4, C17_c4, C17_e1, C17_e2, C17_e3,
       C17_e4, C20_g4, C20_q1, C20_q2, C20_q3, C22_g4, C22_q1, C22_q2, C22_q3, C23_g4, C23_q1, C23_q2,
       C23_q3, CLK, CLR, Cp, dipswitch_1_sw1, dipswitch_1_sw2, dipswitch_1_sw3, dipswitch_1_sw4,
       dipswitch_1_sw5, dipswitch_1_sw6, dipswitch_1_sw7, dipswitch_1_sw8, EA, Ep, Eu, NOT_CE, NOT_CLK,
       NOT_CLR, NOT_E1, NOT_L0, NOT_L1, NOT_LA, NOT_LB, NOT_Lm, READ_WRITE_out, RUN_PROG_sw1, S2_sw1, Su;

  DipSwitch dipswitch_1 (
    .sw1(dipswitch_1_sw1), .sw2(dipswitch_1_sw2), .sw3(dipswitch_1_sw3), .sw4(dipswitch_1_sw4),
    .sw5(dipswitch_1_sw5), .sw6(dipswitch_1_sw6), .sw7(dipswitch_1_sw7), .sw8(dipswitch_1_sw8));
  DipSwitch #(.number(1)) RUN_PROG (.sw1(RUN_PROG_sw1));
  DipSwitch #(.number(4)) A (.sw1(A_sw1), .sw2(A_sw2), .sw3(A_sw3), .sw4(A_sw4));
  and and_1 (and_1_out, NOT_CE, RUN_PROG_sw1);
  Button #(.press("passive")) READ_WRITE (.out(READ_WRITE_out));
  L_74LS107_f74dca52 C2 (
    .CLK1(NOT_CLK), .K1(Cp), .CLR1(NOT_CLR), .J2(Cp), .CLK2(C2_q1), .K2(Cp), .CLR2(NOT_CLR), .J1(Cp),
    .Q1(C2_q1), .Q2(C2_q2));  // open: NOTQ1, NOTQ2
  L_74LS107_f74dca52 C1 (
    .CLK1(C2_q2), .K1(Cp), .CLR1(NOT_CLR), .J2(Cp), .CLK2(C1_q1), .K2(Cp), .CLR2(NOT_CLR), .J1(Cp),
    .Q1(C1_q1), .Q2(C1_q2));  // open: NOTQ1, NOTQ2
  L_74LS173_6bdbcc89 C4 (
    .N(1'b0), .D1(C7_not_do1), .NOT_G1(NOT_Lm), .NOT_G2(NOT_Lm), .D2(C7_not_do2), .CLK(CLK), .D3(C7_not_do3),
    .D4(C7_not_do4), .CLR(1'b0), .M(1'b0), .Q1(C4_q1), .Q2(C4_q2), .Q3(C4_q3), .G4(C4_g4));
  L_74LS157_d074910b C5 (
    .B1(C4_g4), .A2(A_sw2), .B2(C4_q3), .A3(A_sw3), .B3(C4_q2), .A4(A_sw4), .B4(C4_q1), .STROBE_G(1'b0),
    .SELECT_A_B(S2_sw1), .A1(A_sw1), .Y1(C5_y1), .Y2(C5_y2), .Y3(C5_y3), .Y4(C5_y4));
  DipSwitch #(.number(1)) S2 (.sw1(S2_sw1));
  L_74LS189_c76b68cd C7 (
    .A0(C5_y4), .A1(C5_y3), .A2(C5_y2), .A3(C5_y1), .DI1(dipswitch_1_sw4), .DI2(dipswitch_1_sw3),
    .DI3(dipswitch_1_sw2), .DI4(dipswitch_1_sw1), .NOT_S(and_1_out), .NOT_W(READ_WRITE_out),
    .NOT_DO2(C7_not_do2), .NOT_DO3(C7_not_do3), .NOT_DO4(C7_not_do4), .NOT_DO1(C7_not_do1));
  L_74LS189_c76b68cd C6 (
    .A0(C5_y4), .A1(C5_y3), .A2(C5_y2), .A3(C5_y1), .DI1(dipswitch_1_sw8), .DI2(dipswitch_1_sw7),
    .DI3(dipswitch_1_sw6), .DI4(dipswitch_1_sw5), .NOT_S(and_1_out), .NOT_W(READ_WRITE_out),
    .NOT_DO2(C6_not_do2), .NOT_DO3(C6_not_do3), .NOT_DO4(C6_not_do4), .NOT_DO1(C6_not_do1));
  L_74LS173_6bdbcc89 C9 (
    .N(NOT_E1), .D1(C7_not_do1), .NOT_G1(NOT_L1), .NOT_G2(NOT_L1), .D2(C7_not_do2), .CLK(CLK),
    .D3(C7_not_do3), .D4(C7_not_do4), .CLR(1'b0), .M(NOT_E1), .Q1(C7_not_do1), .Q2(C7_not_do2),
    .Q3(C7_not_do3), .G4(C7_not_do4));
  L_74LS173_6bdbcc89 C8 (
    .N(1'b0), .D1(C6_not_do1), .NOT_G1(NOT_L1), .NOT_G2(NOT_L1), .D2(C6_not_do2), .CLK(CLK), .D3(C6_not_do3),
    .D4(C6_not_do4), .CLR(CLR), .M(1'b0), .Q1(C8_q1), .Q2(C8_q2), .Q3(C8_q3), .G4(C8_g4));
  L_74LS126_5b2bd483 C3 (
    .A1(C2_q1), .G1(Ep), .A2(C2_q2), .G2(Ep), .A3(C1_q1), .G3(Ep), .A4(C1_q2), .G4(Ep), .Y1(C7_not_do4),
    .Y2(C7_not_do3), .Y3(C7_not_do2), .Y4(C7_not_do1));
  L_74LS173_6bdbcc89 C11 (
    .N(1'b0), .D1(C7_not_do1), .NOT_G1(NOT_LA), .NOT_G2(NOT_LA), .D2(C7_not_do2), .CLK(CLK), .D3(C7_not_do3),
    .D4(C7_not_do4), .M(1'b0), .Q1(C11_q1), .Q2(C11_q2), .Q3(C11_q3), .G4(C11_g4));  // open: CLR
  L_74LS173_6bdbcc89 C10 (
    .N(1'b0), .D1(C6_not_do1), .NOT_G1(NOT_LA), .NOT_G2(NOT_LA), .D2(C6_not_do2), .CLK(CLK), .D3(C6_not_do3),
    .D4(C6_not_do4), .M(1'b0), .Q1(C10_q1), .Q2(C10_q2), .Q3(C10_q3), .G4(C10_g4));  // open: CLR
  L_74LS83_a67a6f6d C16 (
    .B4(C14_pin3), .A4(C10_q1), .B3(C14_pin6), .A3(C10_q2), .B2(C14_pin8), .A2(C10_q3), .B1(C14_pin11),
    .A1(C10_g4), .C0(C17_c4), .E4(C16_e4), .E3(C16_e4), .E2(C16_e2), .E1(C16_e1));  // open: C4
  _7486 #(.ShowInternalStructure("true")) C14 (
    .pin1(C14_pin1), .pin2(Su), .pin3(C14_pin3), .pin4(C14_pin4), .pin5(Su), .pin6(C14_pin6), .pin13(Su),
    .pin12(C14_pin12), .pin11(C14_pin11), .pin10(Su), .pin9(C14_pin9), .pin8(C14_pin8));
  L_74LS126_5b2bd483 C18 (
    .A1(C16_e4), .G1(Eu), .A2(C16_e4), .G2(Eu), .A3(C16_e2), .G3(Eu), .A4(C16_e1), .G4(Eu), .Y1(C6_not_do1),
    .Y2(C6_not_do2), .Y3(C6_not_do3), .Y4(C6_not_do4));
  L_74LS173_6bdbcc89 C21 (
    .N(1'b0), .D1(C7_not_do1), .NOT_G1(NOT_LB), .NOT_G2(NOT_LB), .D2(C7_not_do2), .CLK(CLK), .D3(C7_not_do3),
    .D4(C7_not_do4), .M(1'b0), .Q1(C14_pin12), .Q2(C14_pin9), .Q3(C14_pin4), .G4(C14_pin1));  // open: CLR
  L_74LS173_6bdbcc89 C20 (
    .N(1'b0), .D1(C6_not_do1), .NOT_G1(NOT_LB), .NOT_G2(NOT_LB), .D2(C6_not_do2), .CLK(CLK), .D3(C6_not_do3),
    .D4(C6_not_do4), .M(1'b0), .Q1(C20_q1), .Q2(C20_q2), .Q3(C20_q3), .G4(C20_g4));  // open: CLR
  L_74LS173_6bdbcc89 C23 (
    .N(1'b0), .D1(C7_not_do1), .NOT_G1(NOT_L0), .NOT_G2(NOT_L0), .D2(C7_not_do2), .CLK(CLK), .D3(C7_not_do3),
    .D4(C7_not_do4), .M(1'b0), .Q1(C23_q1), .Q2(C23_q2), .Q3(C23_q3), .G4(C23_g4));  // open: CLR
  L_74LS173_6bdbcc89 C22 (
    .N(1'b0), .D1(C6_not_do1), .NOT_G1(NOT_L0), .NOT_G2(NOT_L0), .D2(C6_not_do2), .CLK(CLK), .D3(C6_not_do3),
    .D4(C6_not_do4), .M(1'b0), .Q1(C22_q1), .Q2(C22_q2), .Q3(C22_q3), .G4(C22_g4));  // open: CLR
  L_74LS126_5b2bd483 C12 (
    .A1(C11_g4), .G1(EA), .A2(C11_q3), .G2(EA), .A3(C11_q2), .G3(EA), .A4(C11_q1), .G4(EA), .Y1(C7_not_do4),
    .Y2(C7_not_do3), .Y3(C7_not_do2), .Y4(C7_not_do1));
  L_74LS126_5b2bd483 C13 (
    .A1(C10_g4), .G1(EA), .A2(C10_g4), .G2(EA), .A3(C10_g4), .G3(EA), .A4(C10_g4), .G4(EA), .Y1(C6_not_do4),
    .Y2(C6_not_do3), .Y3(C6_not_do2), .Y4(C6_not_do1));
  L_74LS83_a67a6f6d C17 (
    .B4(C15_pin3), .A4(C11_q1), .B3(C15_pin6), .A3(C11_q2), .B2(C15_pin8), .A2(C11_q3), .B1(C15_pin11),
    .A1(C11_g4), .C0(Su), .C4(C17_c4), .E4(C17_e4), .E3(C17_e3), .E2(C17_e2), .E1(C17_e1));
  LedBar ledbar_1 (
    .led0(C22_q1), .led1(C22_q2), .led2(C22_q3), .led3(C22_g4), .led4(C23_q1), .led5(C23_q2), .led6(C23_q3),
    .led7(C23_g4));
  _7486 #(.ShowInternalStructure("true")) C15 (
    .pin1(C20_q1), .pin2(Su), .pin3(C15_pin3), .pin4(C20_q2), .pin5(Su), .pin6(C15_pin6), .pin13(Su),
    .pin12(C20_g4), .pin11(C15_pin11), .pin10(Su), .pin9(C20_q3), .pin8(C15_pin8));
  L_74LS126_5b2bd483 C19 (
    .A1(C17_e4), .G1(Eu), .A2(C17_e3), .G2(Eu), .A3(C17_e2), .G3(Eu), .A4(C17_e1), .G4(Eu), .Y1(C7_not_do1),
    .Y2(C7_not_do2), .Y3(C7_not_do3), .Y4(C7_not_do4));

  // Notes on the sheet:
  //   S2
  //   Instruction Register
  //   RAM
  //   S4
  //   Program Counter
  //   MAR
  //   2 to 1 Multiplexer
  //   Accumulator
  //   B Register
  //   Adder_Subtractor
  //   Ooutput Register
endmodule
